# Fritzing sketch cyclingPusher (saved by Fritzing 0.7.0b)
breadboards: 1

parts:
  Arduino_Ethernet_Shield1 = Arduino Ethernet Shield
  LCD1 = LCD screen
  Q1 = NPN-Transistor [package="TO92 [THT]"]
  R2 = Rotary Potentiometer (Small) [maximum_resistance=100kΩ]
  R3 = Resistor [tolerance=±5% resistance=10k package=THT]
  Reed_Switch = Reed switch [package=THT]
  R1 = Resistor [tolerance=±5% resistance=10k package=THT]
  J1 = Piezo Speaker

nets (from the schematic view):
  N1: Arduino_Ethernet_Shield1.D9, LCD1.DB7
  N2: Arduino_Ethernet_Shield1.D8, LCD1.DB6
  N3: Arduino_Ethernet_Shield1.D7, LCD1.DB5
  N4: Arduino_Ethernet_Shield1.D6, LCD1.DB4
  N5: Arduino_Ethernet_Shield1.D5, LCD1.E
  N6: Arduino_Ethernet_Shield1.SS, LCD1.RS
  N7: Arduino_Ethernet_Shield1.D3, R1.Pin_0
  N8: Arduino_Ethernet_Shield1.D2, R3.Pin_1, Reed_Switch.pin_1
  +5V: Arduino_Ethernet_Shield1.+5V, LCD1.VDD, LCD1.LED+, R2.leg2, Reed_Switch.pin_2
  N9: Arduino_Ethernet_Shield1.GND#20, J1.pin1
  N10: Arduino_Ethernet_Shield1.A0, J1.pin2
  N11: LCD1.VSS, LCD1.R/W, R2.leg1, R3.Pin_0
  N12: LCD1.V0, R2.wiper
  N13: LCD1.LED-, Q1.E
  N14: Q1.B, R1.Pin_1
